// Logisim project hw05.circ as structural Verilog: 4 circuits, main circuit mux2x1_3b
module mux2x1_3b (
  input  [2:0] in1,
  input  [2:0] in0,
  input  s,
  output [2:0] out0
);

  // mux2x1 mux2x1_1: pin names not known; wires that end beside it: in1[0], s, in0[0], out0[0]
  // mux2x1 mux2x1_2: pin names not known; wires that end beside it: in1[1], s, in0[1], out0[1]
  // mux2x1 mux2x1_3: pin names not known; wires that end beside it: in1[2], s, in0[2], out0[2]
endmodule

module add1 (
  input  a,
  input  b,
  input  cin,
  output s,
  output cout
);

  wire and_1_out, and_2_out, and_3_out;

  and and_1 (and_1_out, a, b);
  and and_2 (and_2_out, b, cin);
  and and_3 (and_3_out, a, cin);
  xor xor_1 (s, a, b, cin);
  or or_1 (cout, and_1_out, and_2_out, and_3_out);
endmodule

module ripple_add3_ovf (
  input  [2:0] a,
  input  [2:0] b,
  input  cin,
  output [2:0] s,
  output ovf
);

  wire add1_1_cout, add1_2_cout, add1_3_cout;

  add1 add1_1 (.a(a[0]), .b(b[0]), .cin(cin), .s(s[0]), .cout(add1_1_cout));
  xor xor_1 (ovf, add1_3_cout, add1_2_cout);
  add1 add1_2 (.a(a[1]), .b(b[1]), .cin(add1_1_cout), .s(s[1]), .cout(add1_2_cout));
  add1 add1_3 (.a(a[2]), .b(b[2]), .cin(add1_2_cout), .s(s[2]), .cout(add1_3_cout));
endmodule

module addsub3 (
  input  [2:0] a,
  input  [2:0] b,
  input  sub,
  output [2:0] f,
  output ovf
);

  wire [2:0] mux2x1_3b_1_out0, not_1_out;

  assign not_1_out = ~b;  // NOT_Gate not_1, 3 bits wide
  mux2x1_3b mux2x1_3b_1 (.in1(not_1_out), .in0(b), .s(sub), .out0(mux2x1_3b_1_out0));
  ripple_add3_ovf ripple_add3_ovf_1 (.a(a), .b(mux2x1_3b_1_out0), .cin(sub), .s(f), .ovf(ovf));
endmodule
